# Fritzing sketch SpeakerBonnetCircuit (saved by Fritzing 0.9.3b)

parts:
  Part1 = Adafruit Stereo 3W Speaker Bonnet [part_number="Adafruit #"]
  TRRS1 = Audio Jack (TRRS) 3.5mm [part_number="LUMBERG JEITA RC-5325A" package="RC-5325A [SMD]"]

nets:
  N1: Part1.GPIO13, TRRS1.TIP
  N2: Part1.GND, TRRS1.SLEEVE

custom parts:
  Adafruit Stereo 3W Speaker Bonnet: Hey Mr. DJ! Turn up that Raspberry Pi mix to the max with this cute 3W Stereo Amplifier Bonnet for Raspberry Pi. (It's not big enough to be an official HAT, so we called it a bonnet, you see?) It's the exact same size as a Raspberry Pi Zero but works with any and all Raspberry Pi computers with a 2x20 connector - A+, B+, Zero, Pi 2, Pi 3, etc. This Bonnet uses I2S a digital sound standard, so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
